// Logisim project ControlUnit.circ as structural Verilog
module ControlUnit (
  input  [19:0] in_1
);

  wire ADD, ADDI, AND, ANDI, BEQ, BGE, BGT, BLE, BLT, JUMP, LD, OR, ORI, ST, XOR, XORI;

  Decoder #(.select(4)) decoder_1 (
    .out0(ADD), .out1(ADDI), .out2(AND), .out3(ANDI), .out4(OR), .out5(ORI), .out6(XOR), .out7(XORI),
    .out8(LD), .out9(ST), .out10(JUMP), .out11(BEQ), .out12(BLT), .out13(BGT), .out14(BGE), .out15(BLE),
    .sel(in_1[17:14]), .en(1'b1));

  // Other names for the same wires on the sheet: ADDRESS6[5:0] = in_1[5:0]; ADDRESS10[9:0] = in_1[9:0];
  //   ADDRESS14[13:0] = in_1[13:0]; IMM[5:0] = in_1[5:0]; SRC2[3:0] = in_1[5:2]; OP2[3:0] = in_1[9:6];
  //   SRC1[3:0] = in_1[9:6]; OPCODE[3:0] = in_1[17:14]; DEST[3:0] = in_1[13:10]; OP1[3:0] = in_1[13:10];
  //   SRC[3:0] = in_1[13:10]

  // Notes on the sheet:
  //   First 2 bits are useless
endmodule
